# Fritzing sketch Schematic (saved by Fritzing 0.9.4)
circuit board: 8.46667cm x 5.64444cm
breadboards: 1

parts:
  Mod2 = MKR ENV Shield
  NEOPIXEL1 = Neopixel Strip -- Black (30/m)
  M1 = LLC200D3SH [package=THT]
  JACK1 = 2.1mm DC Barrel Jack
  C1 = Electrolytic Capacitor [package="2cm H-Type"]
  R1 = Resistor [tolerance=±5% resistance=330 package="0402 [SMD]"]
  M2 = DC Motor
  FET2 = STP16NF06 N-Channel Power MOSFET

nets:
  N1: Mod2.D2_PWM, M1.pin2
  N2: Mod2.D3_PWM, R1.Pin_0
  N3: Mod2.D4_PWM, FET2.gate
  GND: Mod2.GND, NEOPIXEL1.GND, M1.pin3, JACK1.switch, C1.-, FET2.source
  VIN: Mod2.VIN, Mod2.5V, NEOPIXEL1.+5V, M1.pin1, JACK1.center, C1.+, M2.pin_1
  N4: NEOPIXEL1.Din, R1.Pin_1
  N5: M2.pin_2, FET2.drain

custom parts:
  MKR ENV Shield: arduino MRK ENV Sheild Atmospheric pressure sensor, temp and humidity, Lux of ambient light, Ultraviolet sensors in MKR form factor.
  Neopixel Strip -- Black (30/m): These NeoPixel strips have 30 digitally-addressable pixel LEDs per meter and are very affordable and are only 12.5 mm wide, 10 mm if you remove the strip from the casing.
  LLC200D3SH: Optomax Digital liquid level switch..
  2.1mm DC Barrel Jack: 2.1mm DC Barrel Jack with Thru-Hole Connectors (breadboardable)
  STP16NF06 N-Channel Power MOSFET: STP16NF06 N-channel Power MOSFET
